// Logisim project A2_Group2.circ as structural Verilog: 1 circuit, main circuit main
// S1
module main (
  input  CS2,
  input  CS1,
  input  CS0,
  input  A3,
  input  A2,
  input  A1,
  input  A0,
  input  B3,
  input  B2,
  input  B1,
  input  B0,
  output Cout,
  output S3,
  output S2,
  output S1,
  output S0,
  output V,
  output Z,
  output S,
  output C
);

  wire Mux_for_X3_x2_p4, Mux_for_X3_x2_p7, Mux_for_X3_x2_p13, Mux_for_X3_x2_p16, Mux_for_y3_y2_p2,
       Mux_for_y3_y2_p11, n7404_1_p4, n7404_1_p6, n7404_1_p10, n7404_1_p12, n7408_1_p11, n7408_1_p14,
       n7432_1_p1, n7432_1_p3, n7432_1_p8, n7432_2_p1, n7483_1_p4, n7483_1_p7, n7483_1_p8, n7483_1_p9,
       n7483_1_p14, n7483_1_p15, n7486_1_p3, n7486_1_p6, n74238_1_p15, n74238_1_p18, n74238_1_p19,
       n74238_1_p20, n74238_1_p21, n74238_1_p22;

  // _7432 7432_1: pin names not known; wires that end beside it: n7432_1_p1, S0, n7432_1_p3, 1'b0, 1'b1, S2, S, n7432_1_p8, n7432_1_p8, S1, n7432_1_p1
  // _74238 74238_1: pin names not known; wires that end beside it: A0, A1, A2, A3, B0, B1, B2, B3, CS0, CS1, CS2, 1'b0, 1'b0, 1'b1, n74238_1_p15, 1'b0, 1'b1, n74238_1_p18, n74238_1_p19, n74238_1_p20, n74238_1_p21, n74238_1_p22
  // _7404 7404_1: pin names not known; wires that end beside it: n7432_1_p3, Z, A2, n7404_1_p4, A1, n7404_1_p6, 1'b0, 1'b1, A3, n7404_1_p10, A0, n7404_1_p12
  // _74153 Mux_for_X3_x2: pin names not known; wires that end beside it: 1'b0, n74238_1_p19, 1'b0, Mux_for_X3_x2_p4, n7404_1_p10, A3, Mux_for_X3_x2_p7, 1'b0, 1'b1, 1'b0, n74238_1_p21, 1'b0, Mux_for_X3_x2_p13, n7404_1_p4, A2, Mux_for_X3_x2_p16
  // _7408 7408_1: pin names not known; wires that end beside it: A3, B3, Mux_for_X3_x2_p4, A2, B2, Mux_for_X3_x2_p13, 1'b0, 1'b1, B1, A1, n7408_1_p11, A0, B0, n7408_1_p14
  // _7483 7483_1: pin names not known; wires that end beside it: Mux_for_X3_x2_p7, S2, Mux_for_X3_x2_p16, n7483_1_p4, 1'b1, S1, n7483_1_p7, n7483_1_p8, n7483_1_p9, S, C, n74238_1_p20, 1'b0, n7483_1_p14, n7483_1_p15, S0
  // _74153 Mux_for_x1_x0: pin names not known; wires that end beside it: 1'b0, n74238_1_p19, 1'b0, n7408_1_p11, n7404_1_p6, A1, n7483_1_p8, 1'b0, 1'b1, 1'b0, n74238_1_p21, 1'b0, n7408_1_p14, n7404_1_p12, A0, n7483_1_p15
  // _74153 Mux_for_y3_y2: pin names not known; wires that end beside it: 1'b0, Mux_for_y3_y2_p2, 1'b0, 1'b1, 1'b0, B3, n7483_1_p9, 1'b0, 1'b1, 1'b0, Mux_for_y3_y2_p11, 1'b0, 1'b1, 1'b0, B2, n7483_1_p4
  // _7432 7432_2: pin names not known; wires that end beside it: n7432_2_p1, n74238_1_p21, Mux_for_y3_y2_p11, n74238_1_p15, n74238_1_p22, Mux_for_y3_y2_p2, 1'b0, 1'b1, n74238_1_p18, n74238_1_p19, n7432_2_p1
  // _74153 Mux_for_Y1_y0: pin names not known; wires that end beside it: 1'b0, Mux_for_y3_y2_p2, 1'b0, 1'b1, 1'b0, B1, n7483_1_p7, 1'b0, 1'b1, 1'b0, Mux_for_y3_y2_p11, 1'b0, 1'b1, 1'b0, B0, n7483_1_p14, CS0, CS1, CS2, A0, A2, A3, B3
  // _7486 7486_1: pin names not known; wires that end beside it: S, Mux_for_X3_x2_p7, n7486_1_p3, n7486_1_p3, n7483_1_p9, n7486_1_p6, 1'b0, 1'b1, n7486_1_p6, C, V

  assign Cout = C;
  assign S3 = S;

  // Notes on the sheet:
  //   a lines, 0 to 3 downward
  //   b lines, 0 to 3 downward
  //   a2'
  //   x3 adder
  //   s lines, 0 to 2 downward
  //   a1'
  //   5
  //   a3'
  //   a3*b3
  //   2
  //   x2 adder
  //   a1*b1
  //   a2*b2
  //   bi
  //   a0'
  //   x1 adder
  //   Cin
  //   12
  //   x0 adder
  //   4
  //   3
  //   6
  //   13
  //   y3
  //   y2
  //   y1
  //   y0
  //   a1
  //   11 to1A
  //   CS2        CS1         CS0        OPERATION
  //   0             0              0              Transfer A
  //   0             0              1               AND
  //   0             1              X               ADD
  //   1             0              0               ADD with carry
  //   1             0              1               Complement A
  //   1             1              X               Decrement A
endmodule
