// Logisim project A2_Group2.circ as structural Verilog: 3 circuits, main circuit main
module main (
  input  [31:0] B,
  input  [31:0] A,
  input  [1:0] in_3,
  output out_4
);

  wire multiplexer_1_out, multiplexer_2_out;
  wire [4:0] bit_extender_4_out;
  wire [11:0] multiplexer_5_out, normalizing_1_exp_out, normalizing_2_exp_out;
  wire [15:0] bit_extender_1_out, final_16_bit_alu_617e8450_1_p2, final_16_bit_alu_617e8450_1_p5,
       multiplexer_6_out, negator_3_out;
  wire [18:0] bit_extender_8_out;
  wire [19:0] bit_extender_2_out, bit_extender_5_out, multiplexer_7_out, multiplexer_8_out, shifter_1_out;
  wire [30:0] adder_1_out;
  wire [31:0] bit_extender_6_out, bit_extender_7_out, multiplexer_3_out, multiplexer_4_out,
       multiplexer_9_out, negator_1_out, negator_2_out, negator_4_out, normalizing_1_frac_out,
       normalizing_2_frac_out;

  Multiplexer multiplexer_1 (
    .in0(A[31]), .in1(B[31]), .out(multiplexer_1_out), .sel(final_16_bit_alu_617e8450_1_p5[15]));  // open: en
  Negator #(.width(32)) negator_1 (.in(bit_extender_7_out), .out(negator_1_out));
  Negator #(.width(32)) negator_2 (.in(bit_extender_6_out), .out(negator_2_out));
  Multiplexer multiplexer_2 (
    .in0(B[31]), .in1(A[31]), .out(multiplexer_2_out), .sel(final_16_bit_alu_617e8450_1_p5[15]));  // open: en
  Multiplexer #(.width(32)) multiplexer_3 (
    .in0(bit_extender_7_out), .in1(negator_1_out), .out(multiplexer_3_out), .sel(multiplexer_1_out));  // open: en
  // Probe on multiplexer_3_out
  // Probe on multiplexer_9_out
  // Probe on final_16_bit_alu_617e8450_1_p5
  Multiplexer #(.width(32)) multiplexer_4 (
    .in0(bit_extender_6_out), .in1(negator_2_out), .out(multiplexer_4_out), .sel(multiplexer_2_out));  // open: en
  assign bit_extender_1_out = {{4{1'b0}}, A[30:19]};  // Bit_Extender bit_extender_1
  // Probe on multiplexer_4_out
  // Final_16_Bit_ALU_617e8450 final_16_bit_alu_617e8450_1: pin names not known; wires that end beside it: bit_extender_1_out, final_16_bit_alu_617e8450_1_p2, in_3, 1'b1, final_16_bit_alu_617e8450_1_p5
  Multiplexer #(.width(12)) multiplexer_5 (
    .in0(A[30:19]), .in1(B[30:19]), .out(multiplexer_5_out), .sel(final_16_bit_alu_617e8450_1_p5[15]));  // open: en
  // Probe on bit_extender_1_out
  assign bit_extender_2_out = {{1{1'b1}}, A[18:0]};  // Bit_Extender bit_extender_2
  // Probe on multiplexer_5_out
  Negator #(.width(16)) negator_3 (.in(final_16_bit_alu_617e8450_1_p5), .out(negator_3_out));
  Multiplexer #(.width(16)) multiplexer_6 (
    .in0(final_16_bit_alu_617e8450_1_p5), .in1(negator_3_out), .out(multiplexer_6_out),
    .sel(final_16_bit_alu_617e8450_1_p5[15]));  // open: en
  assign final_16_bit_alu_617e8450_1_p2 = {{4{1'b0}}, B[30:19]};  // Bit_Extender bit_extender_3
  Multiplexer #(.width(20)) multiplexer_7 (
    .in0(bit_extender_2_out), .in1(bit_extender_5_out), .out(multiplexer_7_out),
    .sel(final_16_bit_alu_617e8450_1_p5[15]));  // open: en
  Bit_Extender #(.in_width(16), .out_width(5), .\type ("zero")) bit_extender_4 (
    .in(multiplexer_6_out), .out(bit_extender_4_out));
  Multiplexer #(.width(20)) multiplexer_8 (
    .in0(bit_extender_5_out), .in1(bit_extender_2_out), .out(multiplexer_8_out),
    .sel(final_16_bit_alu_617e8450_1_p5[15]));  // open: en
  Negator #(.width(32)) negator_4 (.in({out_4, adder_1_out}), .out(negator_4_out));
  assign bit_extender_5_out = {{1{1'b1}}, B[18:0]};  // Bit_Extender bit_extender_5
  // Probe on multiplexer_7_out
  // Probe on multiplexer_8_out
  // Probe on multiplexer_6_out
  // Probe on bit_extender_4_out
  Shifter #(.width(20), .shift("lr")) shifter_1 (
    .in(multiplexer_8_out), .\dist (bit_extender_4_out), .out(shifter_1_out));
  Adder #(.width(32)) adder_1 (
    .a(multiplexer_3_out), .b(multiplexer_4_out), .out({out_4, adder_1_out}));  // open: cin, cout
  Multiplexer #(.width(32)) multiplexer_9 (
    .in0({out_4, adder_1_out}), .in1(negator_4_out), .out(multiplexer_9_out), .sel(out_4));  // open: en
  // Probe on multiplexer_9_out
  // Probe on shifter_1_out
  assign bit_extender_6_out = {{12{1'b0}}, shifter_1_out};  // Bit_Extender bit_extender_6
  // Probe on {out_4, adder_1_out}
  normalizing normalizing_1 (
    .frac(multiplexer_9_out), .exp(multiplexer_5_out), .frac_out(normalizing_1_frac_out),
    .exp_out(normalizing_1_exp_out));
  // Probe on bit_extender_6_out
  assign bit_extender_7_out = {{12{1'b0}}, multiplexer_7_out};  // Bit_Extender bit_extender_7
  normalizing normalizing_2 (
    .frac(normalizing_1_frac_out), .exp(normalizing_1_exp_out), .frac_out(normalizing_2_frac_out),
    .exp_out(normalizing_2_exp_out));
  // Probe on bit_extender_7_out
  // Probe on normalizing_2_exp_out
  // Probe on normalizing_1_frac_out
  // Probe on normalizing_2_frac_out
  Bit_Extender #(.in_width(32), .out_width(19), .\type ("zero")) bit_extender_8 (
    .in(normalizing_2_frac_out), .out(bit_extender_8_out));
  // Probe on bit_extender_8_out

  // Notes on the sheet:
  //   Larger number sign
  //   -L
  //   -S
  //   Smaller number sign
  //   signed L
  //   A exp
  //   A frac
  //   Exponent difference
  //   signed S
  //   Larger exponent
  //   32 bit Significand of the smaller number
  //   32 bit Significand of the larger number
  //   B exp
  //   B frac
  //   Normalization and rounding
  //   Significand of the larger number
  //   Significand of the smaller number
  //   reultant sign bit
  //   Normalization and rounding
  //   resultant exponent
  //   resultant significand
endmodule

module normalizing (
  input  [31:0] frac,
  input  [11:0] exp,
  output [31:0] frac_out,
  output [11:0] exp_out
);

  wire adder_1_cout, bitfinder_1_found, comparator_1_eq, comparator_1_gt, comparator_1_lt, comparator_3_eq,
       comparator_3_lt, comparator_4_eq, comparator_4_gt, subtractor_1_bout, subtractor_3_bout, undriven,
       undriven_2, undriven_3, undriven_4, undriven_5, undriven_6, undriven_7;
  wire [1:0] bit_extender_5_out, bit_extender_7_out, bit_extender_9_out, bit_extender_11_out,
       multiplier_1_out, multiplier_2_out, multiplier_3_out, multiplier_4_out, or_1_out;
  wire [4:0] bitfinder_1_index, multiplexer_3_out, multiplexer_5_out, subtractor_1_out, subtractor_3_out;
  wire [11:0] bit_extender_3_out;
  wire [31:0] bit_extender_1_out, multiplexer_1_out, multiplexer_9_out, negator_1_out, rounding2_1_out_2,
       rounding2_2_out_2, rounding2_3_out_2, shifter_1_out, shifter_3_out, shifter_5_out, shifter_7_out;

  Multiplexer #(.width(32)) multiplexer_1 (
    .in0(bit_extender_1_out), .in1(negator_1_out), .out(multiplexer_1_out), .sel(comparator_1_lt),
    .en(undriven));
  Multiplexer #(.width(32)) multiplexer_2 (
    .in0(bit_extender_1_out), .in1(negator_1_out), .out(multiplexer_1_out), .sel(comparator_1_lt),
    .en(undriven));
  assign bit_extender_1_out = {{27{1'b0}}, subtractor_1_out};  // Bit_Extender bit_extender_1
  assign bit_extender_1_out = {{27{1'b0}}, subtractor_1_out};  // Bit_Extender bit_extender_2
  Negator #(.width(32)) negator_1 (.in(bit_extender_1_out), .out(negator_1_out));
  Negator #(.width(32)) negator_2 (.in(bit_extender_1_out), .out(negator_1_out));
  BitFinder #(.width(32), .\type ("high1")) bitfinder_1 (
    .in(frac), .index(bitfinder_1_index), .found(bitfinder_1_found));
  BitFinder #(.width(32), .\type ("high1")) bitfinder_2 (
    .in(frac), .index(bitfinder_1_index), .found(bitfinder_1_found));
  Comparator #(.width(5)) comparator_1 (
    .a(bitfinder_1_index), .b(5'b10011), .gt(comparator_1_gt), .eq(comparator_1_eq), .lt(comparator_1_lt));
  Comparator #(.width(5)) comparator_2 (
    .a(bitfinder_1_index), .b(5'b10011), .gt(comparator_1_gt), .eq(comparator_1_eq), .lt(comparator_1_lt));
  Multiplexer #(.width(5)) multiplexer_3 (
    .in0(bitfinder_1_index), .in1(5'b10011), .out(multiplexer_3_out), .sel(comparator_1_lt), .en(undriven_2));
  Multiplexer #(.width(5)) multiplexer_4 (
    .in0(bitfinder_1_index), .in1(5'b10011), .out(multiplexer_3_out), .sel(comparator_1_lt), .en(undriven_2));
  Multiplexer #(.width(5)) multiplexer_5 (
    .in0(5'b10011), .in1(bitfinder_1_index), .out(multiplexer_5_out), .sel(comparator_1_lt), .en(undriven_4));
  Multiplexer #(.width(5)) multiplexer_6 (
    .in0(5'b10011), .in1(bitfinder_1_index), .out(multiplexer_5_out), .sel(comparator_1_lt), .en(undriven_4));
  Subtractor #(.width(5)) subtractor_1 (
    .a(multiplexer_3_out), .b(multiplexer_5_out), .out(subtractor_1_out), .bin(undriven_3),
    .bout(subtractor_1_bout));
  Subtractor #(.width(5)) subtractor_2 (
    .a(multiplexer_3_out), .b(multiplexer_5_out), .out(subtractor_1_out), .bin(undriven_3),
    .bout(subtractor_1_bout));
  Shifter #(.width(32)) shifter_1 (.in(frac), .\dist (subtractor_1_out), .out(shifter_1_out));
  Shifter #(.width(32)) shifter_2 (.in(frac), .\dist (subtractor_1_out), .out(shifter_1_out));
  Multiplexer #(.width(32)) multiplexer_7 (
    .in0(multiplexer_9_out), .in1(shifter_1_out), .out(frac_out), .sel(comparator_1_lt), .en(undriven_5));
  Multiplexer #(.width(32)) multiplexer_8 (
    .in0(multiplexer_9_out), .in1(shifter_1_out), .out(frac_out), .sel(comparator_1_lt), .en(undriven_5));
  Bit_Extender #(.in_width(32), .out_width(12), .\type ("zero")) bit_extender_3 (
    .in(multiplexer_1_out), .out(bit_extender_3_out));
  Bit_Extender #(.in_width(32), .out_width(12), .\type ("zero")) bit_extender_4 (
    .in(multiplexer_1_out), .out(bit_extender_3_out));
  // Probe on subtractor_1_out
  // Probe on subtractor_1_out
  Shifter #(.width(32), .shift("lr")) shifter_3 (.in(frac), .\dist (subtractor_3_out), .out(shifter_3_out));
  Shifter #(.width(32), .shift("lr")) shifter_4 (.in(frac), .\dist (subtractor_3_out), .out(shifter_3_out));
  Comparator #(.width(5)) comparator_3 (
    .a(subtractor_1_out), .b(5'b00001), .eq(comparator_3_eq), .lt(comparator_3_lt));  // open: gt
  Comparator #(.width(5)) comparator_4 (
    .a(subtractor_1_out), .b(5'b00010), .gt(comparator_4_gt), .eq(comparator_4_eq));  // open: lt
  Subtractor #(.width(5)) subtractor_3 (
    .a(subtractor_1_out), .b(5'b00011), .out(subtractor_3_out), .bin(undriven_6), .bout(subtractor_3_bout));
  Subtractor #(.width(5)) subtractor_4 (
    .a(subtractor_1_out), .b(5'b00011), .out(subtractor_3_out), .bin(undriven_6), .bout(subtractor_3_bout));
  Adder #(.width(12)) adder_1 (.a(bit_extender_3_out), .b(exp), .out(exp_out), .cin(undriven_7), .cout(adder_1_cout));
  Adder #(.width(12)) adder_2 (.a(bit_extender_3_out), .b(exp), .out(exp_out), .cin(undriven_7), .cout(adder_1_cout));
  Shifter #(.width(32)) shifter_5 (.in(frac), .\dist (5'b00010), .out(shifter_5_out));
  Shifter #(.width(32)) shifter_6 (.in(frac), .\dist (5'b00010), .out(shifter_5_out));
  Shifter #(.width(32)) shifter_7 (.in(frac), .\dist (5'b00001), .out(shifter_7_out));
  Shifter #(.width(32)) shifter_8 (.in(frac), .\dist (5'b00001), .out(shifter_7_out));
  Rounding2 rounding2_1 (.in_1(shifter_3_out), .out_2(rounding2_1_out_2));
  Rounding2 rounding2_2 (.in_1(shifter_5_out), .out_2(rounding2_2_out_2));
  Rounding2 rounding2_3 (.in_1(shifter_7_out), .out_2(rounding2_3_out_2));
  assign bit_extender_5_out = {{1{1'b0}}, comparator_3_lt};  // Bit_Extender bit_extender_5
  assign bit_extender_5_out = {{1{1'b0}}, comparator_3_lt};  // Bit_Extender bit_extender_6
  assign bit_extender_7_out = {{1{1'b0}}, comparator_3_eq};  // Bit_Extender bit_extender_7
  assign bit_extender_7_out = {{1{1'b0}}, comparator_3_eq};  // Bit_Extender bit_extender_8
  assign bit_extender_9_out = {{1{1'b0}}, comparator_4_eq};  // Bit_Extender bit_extender_9
  assign bit_extender_9_out = {{1{1'b0}}, comparator_4_eq};  // Bit_Extender bit_extender_10
  assign bit_extender_11_out = {{1{1'b0}}, comparator_4_gt};  // Bit_Extender bit_extender_11
  assign bit_extender_11_out = {{1{1'b0}}, comparator_4_gt};  // Bit_Extender bit_extender_12
  // Probe on bit_extender_5_out
  // Probe on bit_extender_7_out
  // Probe on bit_extender_9_out
  // Probe on bit_extender_11_out
  Multiplier #(.width(2)) multiplier_1 (.a(bit_extender_5_out), .b(2'b00), .out(multiplier_1_out));  // open: cin, cout
  Multiplier #(.width(2)) multiplier_2 (.a(bit_extender_7_out), .b(2'b01), .out(multiplier_2_out));  // open: cin, cout
  Multiplier #(.width(2)) multiplier_3 (.a(bit_extender_9_out), .b(2'b10), .out(multiplier_3_out));  // open: cin, cout
  Multiplier #(.width(2)) multiplier_4 (.a(bit_extender_11_out), .b(2'b11), .out(multiplier_4_out));  // open: cin, cout
  assign or_1_out = multiplier_1_out | multiplier_2_out | multiplier_3_out | multiplier_4_out;  // OR_Gate or_1, 2 bits wide
  // Probe on multiplexer_9_out
  Multiplexer #(.select(2), .width(32), .enable("false")) multiplexer_9 (
    .in0(frac), .in1(rounding2_2_out_2), .in2(rounding2_3_out_2), .in3(rounding2_1_out_2),
    .out(multiplexer_9_out), .sel(or_1_out));
  // Probe on or_1_out

  // Notes on the sheet:
  //   if 0, then right shift
endmodule

module Rounding2 (
  input  [31:0] in_1,
  output [31:0] out_2
);

  wire [31:0] adder_1_out, adder_2_out, bit_extender_1_out, shifter_1_out, shifter_2_out;

  Shifter #(.width(32), .shift("lr")) shifter_1 (.in(in_1), .\dist (5'b00011), .out(shifter_1_out));
  assign bit_extender_1_out = {{31{1'b0}}, in_1[3]};  // Bit_Extender bit_extender_1
  Multiplexer #(.select(3), .width(32)) multiplexer_1 (
    .in0(shifter_1_out), .in1(shifter_1_out), .in2(shifter_1_out), .in3(shifter_1_out), .in4(adder_1_out),
    .in5(adder_2_out), .in6(adder_2_out), .in7(adder_2_out), .out(out_2), .sel(in_1[2:0]));  // open: en
  Shifter #(.width(32), .shift("lr")) shifter_2 (.in(in_1), .\dist (5'b00011), .out(shifter_2_out));
  Adder #(.width(32)) adder_1 (.a(bit_extender_1_out), .b(shifter_2_out), .out(adder_1_out));  // open: cin, cout
  Adder #(.width(32)) adder_2 (.a(shifter_2_out), .b(32'h1), .out(adder_2_out));  // open: cin, cout
endmodule
